# Fritzing sketch wiring (saved by Fritzing 0.9.3b)
breadboards: 1

parts:
  LED1 = smd LED [color="Red (633nm)" package="1206 [SMD]"]
  S5 = Pushbutton [package="[THT]"]
  R1 = PHOTOCELL [package=photocell]
  R2 = Resistor [tolerance=±5% resistance=330 package="2010 [SMD]"]
  R3 = Resistor [tolerance=±5% resistance=10k package="0402 [SMD]"]
  SERVO1 = Tower Pro SG90 servo [part_number=101246]
  R4 = Resistor [tolerance=±5% resistance=10k package="0402 [SMD]"]
  Part1 = Arduino MKR WIFI 1010  # not connected
  DHT1 = DHT11 Humitidy and Temperature Sensor

nets:
  N1: LED1.cathode, R2.Pin_0
  N2: S5.Pin_1, S5.Pin_2
  N3: S5.Pin_3, S5.Pin_4, R1.P$2, R4.Pin_1, DHT1.VDD
  N4: R1.P$1, R3.Pin_0
  GND: R2.Pin_1, R3.Pin_1, SERVO1.GND, DHT1.GND
  N5: R4.Pin_0, DHT1.DATA

custom parts:
  Tower Pro SG90 servo: Original file by John De Cristofaro http://www.adafruit.com/products/1449 Adafruit Feedback Servo (Small) Edited by: e-radionica.com 28/9/2015
  Arduino MKR WIFI 1010: The MKR WIFI 1010 is a significant improvement on the MKR 1000 WIFI. It's equipped with an ESP32 module made by U-BLOX. This board aims to speed up and simplify the prototyping of WiFi based IoT applications thanks to the flexibility of the ESP32 module and its low power consumption. The board is composed of three main blocks: SAMD21 Cortex-M0+ 32bit Low Power ARM MCU; U-BLOX NINA-W10 Series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
  DHT11 Humitidy and Temperature Sensor: DHT11 Humidity and Temperature Sensor
